// Logisim project adder.circ as structural Verilog: 2 circuits, main circuit 16-bit ripple adder
module _16_bit_ripple_adder (
  input  [15:0] A,
  input  sub,
  input  [15:0] B,
  output [15:0] result,
  output ovf
);

  wire C0, C1, C2, C3, C4, C5, C6, C7, C8, C9, C10, C11, C12, C13, C14, C15, cin, cout, LSB_cout,
       n1_bit_full_adder_1_cout, n1_bit_full_adder_2_cout, n1_bit_full_adder_3_cout,
       n1_bit_full_adder_4_cout, n1_bit_full_adder_5_cout, n1_bit_full_adder_6_cout,
       n1_bit_full_adder_7_cout, n1_bit_full_adder_8_cout, n1_bit_full_adder_9_cout,
       n1_bit_full_adder_10_cout, n1_bit_full_adder_11_cout, n1_bit_full_adder_12_cout,
       n1_bit_full_adder_13_cout;

  _1_bit_full_adder LSB (.Cin(sub), .A(A[0]), .B(C0), .Sum(result[0]), .Cout(LSB_cout));
  _1_bit_full_adder u_1_bit_full_adder_1 (
    .Cin(LSB_cout), .A(A[1]), .B(C1), .Sum(result[1]), .Cout(n1_bit_full_adder_1_cout));
  _1_bit_full_adder u_1_bit_full_adder_2 (
    .Cin(n1_bit_full_adder_1_cout), .A(A[2]), .B(C2), .Sum(result[2]), .Cout(n1_bit_full_adder_2_cout));
  _1_bit_full_adder u_1_bit_full_adder_3 (
    .Cin(n1_bit_full_adder_2_cout), .A(A[3]), .B(C3), .Sum(result[3]), .Cout(n1_bit_full_adder_3_cout));
  _1_bit_full_adder u_1_bit_full_adder_4 (
    .Cin(n1_bit_full_adder_3_cout), .A(A[4]), .B(C4), .Sum(result[4]), .Cout(n1_bit_full_adder_4_cout));
  _1_bit_full_adder u_1_bit_full_adder_5 (
    .Cin(n1_bit_full_adder_4_cout), .A(A[5]), .B(C5), .Sum(result[5]), .Cout(n1_bit_full_adder_5_cout));
  _1_bit_full_adder u_1_bit_full_adder_6 (
    .Cin(n1_bit_full_adder_5_cout), .A(A[6]), .B(C6), .Sum(result[6]), .Cout(n1_bit_full_adder_6_cout));
  _1_bit_full_adder u_1_bit_full_adder_7 (
    .Cin(n1_bit_full_adder_6_cout), .A(A[7]), .B(C7), .Sum(result[7]), .Cout(n1_bit_full_adder_7_cout));
  _1_bit_full_adder u_1_bit_full_adder_8 (
    .Cin(n1_bit_full_adder_7_cout), .A(A[8]), .B(C8), .Sum(result[8]), .Cout(n1_bit_full_adder_8_cout));
  _1_bit_full_adder u_1_bit_full_adder_9 (
    .Cin(n1_bit_full_adder_8_cout), .A(A[9]), .B(C9), .Sum(result[9]), .Cout(n1_bit_full_adder_9_cout));
  _1_bit_full_adder u_1_bit_full_adder_10 (
    .Cin(n1_bit_full_adder_9_cout), .A(A[10]), .B(C10), .Sum(result[10]), .Cout(n1_bit_full_adder_10_cout));
  _1_bit_full_adder u_1_bit_full_adder_11 (
    .Cin(n1_bit_full_adder_10_cout), .A(A[11]), .B(C11), .Sum(result[11]), .Cout(n1_bit_full_adder_11_cout));
  _1_bit_full_adder u_1_bit_full_adder_12 (
    .Cin(n1_bit_full_adder_11_cout), .A(A[12]), .B(C12), .Sum(result[12]), .Cout(n1_bit_full_adder_12_cout));
  _1_bit_full_adder u_1_bit_full_adder_13 (
    .Cin(n1_bit_full_adder_12_cout), .A(A[13]), .B(C13), .Sum(result[13]), .Cout(n1_bit_full_adder_13_cout));
  _1_bit_full_adder u_1_bit_full_adder_14 (
    .Cin(n1_bit_full_adder_13_cout), .A(A[14]), .B(C14), .Sum(result[14]), .Cout(cin));
  _1_bit_full_adder u_1_bit_full_adder_15 (.Cin(cin), .A(A[15]), .B(C15), .Sum(result[15]), .Cout(cout));
  xor XOR (C0, sub, B[0]);
  xor XOR_2 (C4, sub, B[4]);
  xor XOR_3 (C8, sub, B[8]);
  xor XOR_4 (C12, sub, B[12]);
  xor XOR_5 (C1, sub, B[1]);
  xor XOR_6 (C5, sub, B[5]);
  xor XOR_7 (C9, sub, B[9]);
  xor XOR_8 (C13, sub, B[13]);
  xor XOR_9 (C2, sub, B[2]);
  xor XOR_10 (C6, sub, B[6]);
  xor XOR_11 (C10, sub, B[10]);
  xor XOR_12 (C14, sub, B[14]);
  xor XOR_13 (C3, sub, B[3]);
  xor XOR_14 (C7, sub, B[7]);
  xor XOR_15 (C11, sub, B[11]);
  xor XOR_16 (C15, sub, B[15]);
  xor XOR_17 (ovf, cout, cin);

  // Other names for the same wires on the sheet: S0 = result[0]; S1 = result[1]; S2 = result[2]; S3 = result[3];
  //   S4 = result[4]; S5 = result[5]; S6 = result[6]; S7 = result[7]; S8 = result[8]; S9 = result[9];
  //   S10 = result[10]; S11 = result[11]; S12 = result[12]; S13 = result[13]; S14 = result[14]; S15 = result[15]
endmodule

module _1_bit_full_adder (
  input  Cin,
  input  A,
  input  B,
  output Sum,
  output Cout
);

  wire A_B_out, and_1_out, xor_1_out;

  xor xor_1 (xor_1_out, A, B);
  and A_B (A_B_out, B, A);
  xor xor_2 (Cout, and_1_out, A_B_out);
  xor xor_3 (Sum, Cin, xor_1_out);
  and and_1 (and_1_out, xor_1_out, Cin);
endmodule
