// Logisim project circuit1.circ as structural Verilog: 1 circuit, main circuit main
module main (
  input  A,
  input  B,
  input  C,
  output out
);

  wire A__B_C_out, A_B_out, B_C_2_out, B_C_out, OR_out;

  and A_B (A_B_out, A, B);
  or B_C (B_C_out, B, C);
  and B_C_2 (B_C_2_out, B, C);
  and A__B_C (A__B_C_out, A, B_C_out);
  or OR (OR_out, A_B_out, B_C_2_out);
  or OR_2 (out, A__B_C_out, OR_out);
endmodule
