// Logisim project circuit2.circ as structural Verilog: 1 circuit, main circuit main
module main (
  input  A,
  input  B,
  input  C,
  output out1,
  output out2
);

  wire A_B_C_out, B_nC_out, nA_C_out, nA_nB_out, nB_C_out, not_1_out, not_2_out, not_3_out;

  not not_1 (not_1_out, A);
  not not_2 (not_2_out, C);
  and nA_nB (nA_nB_out, not_1_out, not_3_out);
  and A_B_C (A_B_C_out, A, B, C);
  and nA_C (nA_C_out, not_1_out, C);
  not not_3 (not_3_out, B);
  and nB_C (nB_C_out, not_3_out, C);
  and B_nC (B_nC_out, B, not_2_out);
  or OR (out1, nA_nB_out, A_B_C_out);
  or OR_2 (out2, nA_C_out, nB_C_out, B_nC_out);
endmodule
