// Logisim project fsm.circ as structural Verilog: 1 circuit, main circuit main
module main (
  input  in1,
  input  in2,
  output out
);

  wire clock_1_out, D0_out, D1_out, not_1_out, not_2_out, not_3_out, not_4_out, not_5_out, not_6_out, nQ0,
       nQ1, nQ1_in1_nin2_out, nQ1_nin1_in2_out, nQ1_Q0_nin1_in2_out, Q0, Q0_in1_nin2_2_out, Q0_in1_nin2_out,
       Q0_nin1_in2_out, Q1, Q1_Q0_in1_out;

  Clock clock_1 (.out(clock_1_out));
  and Q1_Q0_in1 (Q1_Q0_in1_out, Q1, Q0, in1);
  and nQ1_Q0_nin1_in2 (nQ1_Q0_nin1_in2_out, nQ1, Q0, not_1_out, in2);
  not not_1 (not_1_out, in1);
  and Q0_in1_nin2 (Q0_in1_nin2_out, Q0, in1, not_2_out);
  not not_2 (not_2_out, in2);
  and nQ1_in1_nin2 (nQ1_in1_nin2_out, nQ1, in1, not_3_out);
  not not_3 (not_3_out, in2);
  and nQ1_nin1_in2 (nQ1_nin1_in2_out, nQ1, not_4_out, in2);
  not not_4 (not_4_out, in1);
  and Q0_in1_nin2_2 (Q0_in1_nin2_2_out, Q0, in1, not_5_out);
  not not_5 (not_5_out, in2);
  not not_6 (not_6_out, in1);
  and Q0_nin1_in2 (Q0_nin1_in2_out, Q0, not_6_out, in2);
  or D1 (D1_out, Q1_Q0_in1_out, nQ1_Q0_nin1_in2_out, Q0_in1_nin2_out);
  or D0 (D0_out, nQ1_in1_nin2_out, nQ1_nin1_in2_out, Q0_in1_nin2_2_out, Q0_nin1_in2_out);
  D_Flip_Flop D1_Q1 (.clk(clock_1_out), .D(D1_out), .Q(Q1), .Qn(nQ1));  // open: preset, en, reset
  D_Flip_Flop D0_Q0 (.clk(clock_1_out), .D(D0_out), .Q(Q0), .Qn(nQ0));  // open: preset, en, reset
  and and_1 (out, Q1, Q0);
endmodule
